// Digital circuit ALU.dig as structural Verilog
module ALU (
  input  [7:0] A,
  input  SUB,
  input  [7:0] B,
  input  [2:0] OPCODE_Princi,
  input  OPCODE,
  input  GRAVAR,
  input  clk,
  output Cout,
  output [7:0] RESULTADO,
  output [7:0] MQ,
  output [7:0] RESULTADO_REG
);

  wire _1, _2, _3, _4, _5, _6, _7, N0, N1, N2, N3, N4, N5, N6, N7, Q0, Q1, Q2, Q3, Q4, Q5, Q6, Q7, S0, S1,
       S2, S3, S4, S5, S6, S7, somador_16bit_1_cout, somador_16bit_2_cout, somador_16bit_3_cout,
       somador_16bit_4_cout, somador_16bit_5_cout, somador_16bit_6_cout, X0, X1, X2, X3, X4, X5, X6, X7,
       xor_1_out, xor_2_out, xor_3_out, xor_4_out, xor_5_out, xor_6_out, xor_7_out, xor_8_out;
  wire [7:0] P1, P2, PP0, PP1, PP2, PP3, PP4, PP5, PP6, PP7;
  wire [15:0] R_OUT1, R_OUT2, R_OUT3, R_OUT4, R_OUT5, R_OUT6, R_OUT7, R_OUT8, somador_16bit_1_s,
       somador_16bit_2_s, somador_16bit_3_s, somador_16bit_4_s, somador_16bit_5_s, somador_16bit_6_s;

  and and_1 (PP0[0], A[0], B[0]);
  and and_2 (PP0[1], A[1], B[0]);
  and and_3 (PP0[2], A[2], B[0]);
  and and_4 (PP0[3], A[3], B[0]);
  and and_5 (PP0[4], A[4], B[0]);
  and and_6 (PP0[5], A[5], B[0]);
  and and_7 (PP0[6], A[6], B[0]);
  and and_8 (PP0[7], A[7], B[0]);
  and and_9 (PP1[0], A[0], B[1]);
  and and_10 (PP1[1], A[1], B[1]);
  and and_11 (PP1[2], A[2], B[1]);
  and and_12 (PP1[3], A[3], B[1]);
  and and_13 (PP1[4], A[4], B[1]);
  and and_14 (PP1[5], A[5], B[1]);
  and and_15 (PP1[6], A[6], B[1]);
  and and_16 (PP1[7], A[7], B[1]);
  EstagioDivisao estagiodivisao_1 (.R_IN({16{1'b0}}), .B_IN({{8{1'b0}}, B}), .A_BIT(A[7]), .R_OUT(R_OUT1), .Q_BIT(Q7));
  EstagioDivisao estagiodivisao_2 (.R_IN(R_OUT1), .B_IN({{8{1'b0}}, B}), .A_BIT(A[6]), .R_OUT(R_OUT2), .Q_BIT(Q6));
  EstagioDivisao estagiodivisao_3 (.R_IN(R_OUT2), .B_IN({{8{1'b0}}, B}), .A_BIT(A[5]), .R_OUT(R_OUT3), .Q_BIT(Q5));
  EstagioDivisao estagiodivisao_4 (.R_IN(R_OUT3), .B_IN({{8{1'b0}}, B}), .A_BIT(A[4]), .R_OUT(R_OUT4), .Q_BIT(Q4));
  EstagioDivisao estagiodivisao_5 (.R_IN(R_OUT4), .B_IN({{8{1'b0}}, B}), .A_BIT(A[3]), .R_OUT(R_OUT5), .Q_BIT(Q3));
  EstagioDivisao estagiodivisao_6 (.R_IN(R_OUT5), .B_IN({{8{1'b0}}, B}), .A_BIT(A[2]), .R_OUT(R_OUT6), .Q_BIT(Q2));
  EstagioDivisao estagiodivisao_7 (.R_IN(R_OUT6), .B_IN({{8{1'b0}}, B}), .A_BIT(A[1]), .R_OUT(R_OUT7), .Q_BIT(Q1));
  EstagioDivisao estagiodivisao_8 (.R_IN(R_OUT7), .B_IN({{8{1'b0}}, B}), .A_BIT(A[0]), .R_OUT(R_OUT8), .Q_BIT(Q0));
  and and_17 (PP2[0], A[0], B[2]);
  and and_18 (PP2[1], A[1], B[2]);
  and and_19 (PP2[2], A[2], B[2]);
  and and_20 (PP2[3], A[3], B[2]);
  and and_21 (PP2[4], A[4], B[2]);
  and and_22 (PP2[5], A[5], B[2]);
  and and_23 (PP2[6], A[6], B[2]);
  and and_24 (PP2[7], A[7], B[2]);
  somador_16bit somador_16bit_1 (
    .A({{8{1'b0}}, PP0}), .B({{7{1'b0}}, PP1, 1'b0}), .CIN(1'b0), .COUT(somador_16bit_1_cout),
    .S(somador_16bit_1_s));
  somador_16bit somador_16bit_2 (
    .A(somador_16bit_1_s), .B({{6{1'b0}}, PP2, 2'b00}), .CIN(somador_16bit_1_cout),
    .COUT(somador_16bit_2_cout), .S(somador_16bit_2_s));
  xor xor_1 (xor_1_out, SUB, B[7]);
  somador_16bit somador_16bit_3 (
    .A(somador_16bit_2_s), .B({{5{1'b0}}, PP3, 3'b000}), .CIN(somador_16bit_2_cout),
    .COUT(somador_16bit_3_cout), .S(somador_16bit_3_s));
  full_adder full_adder_1 (.A(A[7]), .B(xor_1_out), .Cin(_7), .S(S7), .Cout(Cout));
  xor xor_2 (xor_2_out, SUB, B[6]);
  somador_16bit somador_16bit_4 (
    .A(somador_16bit_3_s), .B({4'b0000, PP4, 4'b0000}), .CIN(somador_16bit_3_cout),
    .COUT(somador_16bit_4_cout), .S(somador_16bit_4_s));
  and and_25 (PP3[0], A[0], B[3]);
  and and_26 (PP3[1], A[1], B[3]);
  and and_27 (PP3[2], A[2], B[3]);
  and and_28 (PP3[3], A[3], B[3]);
  and and_29 (PP3[4], A[4], B[3]);
  and and_30 (PP3[5], A[5], B[3]);
  and and_31 (PP3[6], A[6], B[3]);
  and and_32 (PP3[7], A[7], B[3]);
  full_adder full_adder_2 (.A(A[6]), .B(xor_2_out), .Cin(_6), .S(S6), .Cout(_7));
  somador_16bit somador_16bit_5 (
    .A(somador_16bit_4_s), .B({3'b000, PP5, {5{1'b0}}}), .CIN(somador_16bit_4_cout),
    .COUT(somador_16bit_5_cout), .S(somador_16bit_5_s));
  xor xor_3 (xor_3_out, SUB, B[5]);
  full_adder full_adder_3 (.A(A[5]), .B(xor_3_out), .Cin(_5), .S(S5), .Cout(_6));
  somador_16bit somador_16bit_6 (
    .A(somador_16bit_5_s), .B({2'b00, PP6, {6{1'b0}}}), .CIN(somador_16bit_5_cout),
    .COUT(somador_16bit_6_cout), .S(somador_16bit_6_s));
  somador_16bit somador_16bit_7 (
    .A(somador_16bit_6_s), .B({1'b0, PP7, {7{1'b0}}}), .CIN(somador_16bit_6_cout), .S({P2, P1}));  // open: COUT
  xor xor_4 (xor_4_out, SUB, B[4]);
  full_adder full_adder_4 (.A(A[4]), .B(xor_4_out), .Cin(_4), .S(S4), .Cout(_5));
  Multiplexer #(.Selector_Bits(3), .Bits(8)) multiplexer_1 (
    .sel(OPCODE_Princi), .in_0({S7, S6, S5, S4, S3, S2, S1, S0}), .in_1({X7, X6, X5, X4, X3, X2, X1, X0}),
    .in_2({N7, N6, N5, N4, N3, N2, N1, N0}), .in_3({A[6:0], 1'b0}), .in_4({1'b0, A[7:1]}), .in_5(P1),
    .in_6({Q7, Q6, Q5, Q4, Q3, Q2, Q1, Q0}), .in_7({8{1'b0}}), .out(RESULTADO));
  Register #(.Bits(8)) register_1 (.D(RESULTADO), .C(clk), .en(GRAVAR), .Q(RESULTADO_REG));
  xor xor_5 (xor_5_out, SUB, B[3]);
  full_adder full_adder_5 (.A(A[3]), .B(xor_5_out), .Cin(_3), .S(S3), .Cout(_4));
  and and_33 (PP4[0], A[0], B[4]);
  and and_34 (PP4[1], A[1], B[4]);
  and and_35 (PP4[2], A[2], B[4]);
  and and_36 (PP4[3], A[3], B[4]);
  and and_37 (PP4[4], A[4], B[4]);
  and and_38 (PP4[5], A[5], B[4]);
  and and_39 (PP4[6], A[6], B[4]);
  and and_40 (PP4[7], A[7], B[4]);
  xor xor_6 (xor_6_out, SUB, B[2]);
  full_adder full_adder_6 (.A(A[2]), .B(xor_6_out), .Cin(_2), .S(S2), .Cout(_3));
  xor xor_7 (xor_7_out, SUB, B[1]);
  Multiplexer #(.Bits(8)) multiplexer_2 (.sel(OPCODE), .in_0(P2), .in_1(R_OUT8[7:0]), .out(MQ));
  full_adder full_adder_7 (.A(A[1]), .B(xor_7_out), .Cin(_1), .S(S1), .Cout(_2));
  xor xor_8 (xor_8_out, SUB, B[0]);
  full_adder full_adder_8 (.A(A[0]), .B(xor_8_out), .Cin(SUB), .S(S0), .Cout(_1));
  and and_41 (PP5[0], A[0], B[5]);
  and and_42 (PP5[1], A[1], B[5]);
  and and_43 (PP5[2], A[2], B[5]);
  and and_44 (PP5[3], A[3], B[5]);
  and and_45 (PP5[4], A[4], B[5]);
  and and_46 (PP5[5], A[5], B[5]);
  and and_47 (PP5[6], A[6], B[5]);
  and and_48 (PP5[7], A[7], B[5]);
  nand nand_1 (N7, A[7], B[7]);
  nand nand_2 (N6, A[6], B[6]);
  nand nand_3 (N5, A[5], B[5]);
  nand nand_4 (N4, A[4], B[4]);
  nand nand_5 (N3, A[3], B[3]);
  nand nand_6 (N2, A[2], B[2]);
  nand nand_7 (N1, A[1], B[1]);
  and and_49 (PP6[0], A[0], B[6]);
  and and_50 (PP6[1], A[1], B[6]);
  and and_51 (PP6[2], A[2], B[6]);
  and and_52 (PP6[3], A[3], B[6]);
  and and_53 (PP6[4], A[4], B[6]);
  and and_54 (PP6[5], A[5], B[6]);
  and and_55 (PP6[6], A[6], B[6]);
  and and_56 (PP6[7], A[7], B[6]);
  nand nand_8 (N0, A[0], B[0]);
  xor xor_9 (X7, A[7], B[7]);
  xor xor_10 (X6, A[6], B[6]);
  xor xor_11 (X5, A[5], B[5]);
  xor xor_12 (X4, A[4], B[4]);
  xor xor_13 (X3, A[3], B[3]);
  and and_57 (PP7[0], A[0], B[7]);
  and and_58 (PP7[1], A[1], B[7]);
  and and_59 (PP7[2], A[2], B[7]);
  and and_60 (PP7[3], A[3], B[7]);
  and and_61 (PP7[4], A[4], B[7]);
  and and_62 (PP7[5], A[5], B[7]);
  and and_63 (PP7[6], A[6], B[7]);
  and and_64 (PP7[7], A[7], B[7]);
  xor xor_14 (X2, A[2], B[2]);
  xor xor_15 (X1, A[1], B[1]);
  xor xor_16 (X0, A[0], B[0]);

  // Other names for the same wires on the sheet: PR2[9:2] = PP2; PR3[10:3] = PP3; PR4[11:4] = PP4; PR5[12:5] = PP5;
  //   PR6[13:6] = PP6; PR7[14:7] = PP7; PR1[8:1] = PP1; PR0[7:0] = PP0; B_16[7:0] = B; SOBRA[7:0] = R_OUT8[15:8];
  //   RS1[7:0] = RESULTADO
endmodule
