// Digital circuit CPU.dig as structural Verilog
module CPU (
  input  clk,
  input  in_3,
  input  in_4,
  input  in_5,
  output out_2,
  output [7:0] out_6,
  output out_7,
  output [7:0] out_8,
  output [7:0] out_9
);

  wire d_ff_1_q, d_ff_2_q, d_ff_3_q, or_1_out, T0, T1, T2;
  wire [2:0] _3bit;
  wire [4:0] grn;
  wire [7:0] alu_1_mq, counter_1_out, D, resulta;

  ALU alu_1 (
    .A(out_6), .SUB(in_3), .B(D), .OPCODE_Princi(_3bit), .OPCODE(in_4), .GRAVAR(in_5), .clk(clk),
    .Cout(out_7), .RESULTADO(out_8), .MQ(alu_1_mq), .RESULTADO_REG(resulta));
  or or_1 (or_1_out, T0, T2);
  Counter #(.Bits(8)) counter_1 (.en(or_1_out), .C(clk), .clr(1'b0), .out(counter_1_out), .ovf(out_2));
  Register #(.Bits(8)) register_1 (.D(out_8), .C(clk), .en(T2), .Q(out_6));
  Register #(.Bits(8)) register_2 (.D(alu_1_mq), .C(clk), .en(T2), .Q(out_9));
  D_FF #(.Default(1)) d_ff_1 (.D(d_ff_3_q), .C(clk), .Q(d_ff_1_q), .nQ(T0));
  ROM #(.AddrBits(8), .Bits(8)) rom_1 (.A(counter_1_out), .sel(1'b1), .D(D));
  D_FF d_ff_2 (.D(d_ff_1_q), .C(clk), .Q(d_ff_2_q), .nQ(T1));
  Register #(.Bits(8)) register_3 (.D(D), .C(clk), .en(T0), .Q({grn, _3bit}));
  D_FF d_ff_3 (.D(d_ff_2_q), .C(clk), .Q(d_ff_3_q), .nQ(T2));

  // Other names for the same wires on the sheet: MQ[7:0] = out_9; QA[7:0] = out_6; resultado[7:0] = out_8

  // Notes on the sheet:
  //   contents of rom_1 (hex, n*v repeats v):
  //   0,2,0,5
endmodule
