// Digital circuit EstagioDivisao.dig as structural Verilog
module EstagioDivisao (
  input  [15:0] R_IN,
  input  [15:0] B_IN,
  input  A_BIT,
  output [15:0] R_OUT,
  output Q_BIT
);

  wire [15:0] not_1_out, somador_16bit_1_s;

  assign not_1_out = ~B_IN;  // Not not_1, 16 bits wide
  somador_16bit somador_16bit_1 (
    .A({R_IN[14:0], A_BIT}), .B(not_1_out), .CIN(1'b1), .COUT(Q_BIT), .S(somador_16bit_1_s));
  Multiplexer #(.Bits(16)) multiplexer_1 (
    .sel(Q_BIT), .in_0({R_IN[14:0], A_BIT}), .in_1(somador_16bit_1_s), .out(R_OUT));

  // Other names for the same wires on the sheet: R_SHIFT[15:0] = {R_IN[14:0], A_BIT}
endmodule
