// Digital circuit somador 16bit.dig as structural Verilog
module somador_16bit (
  input  [15:0] A,
  input  [15:0] B,
  input  CIN,
  output COUT,
  output [15:0] S
);

  wire _1, _2, _3, _4, _5, _6, _7, _8, _9, _10, _11, _12, _13, _14, full_adder_2_cout;

  full_adder full_adder_1 (.A(A[8]), .B(B[8]), .Cin(full_adder_2_cout), .S(S[8]), .Cout(_8));
  full_adder full_adder_2 (.A(A[7]), .B(B[7]), .Cin(_7), .S(S[7]), .Cout(full_adder_2_cout));
  full_adder full_adder_3 (.A(A[9]), .B(B[9]), .Cin(_8), .S(S[9]), .Cout(_9));
  full_adder full_adder_4 (.A(A[6]), .B(B[6]), .Cin(_6), .S(S[6]), .Cout(_7));
  full_adder full_adder_5 (.A(A[10]), .B(B[10]), .Cin(_9), .S(S[10]), .Cout(_10));
  full_adder full_adder_6 (.A(A[5]), .B(B[5]), .Cin(_5), .S(S[5]), .Cout(_6));
  full_adder full_adder_7 (.A(A[11]), .B(B[11]), .Cin(_10), .S(S[11]), .Cout(_11));
  full_adder full_adder_8 (.A(A[4]), .B(B[4]), .Cin(_4), .S(S[4]), .Cout(_5));
  full_adder full_adder_9 (.A(A[12]), .B(B[12]), .Cin(_11), .S(S[12]), .Cout(_12));
  full_adder full_adder_10 (.A(A[3]), .B(B[3]), .Cin(_3), .S(S[3]), .Cout(_4));
  full_adder full_adder_11 (.A(A[13]), .B(B[13]), .Cin(_12), .S(S[13]), .Cout(_13));
  full_adder full_adder_12 (.A(A[2]), .B(B[2]), .Cin(_2), .S(S[2]), .Cout(_3));
  full_adder full_adder_13 (.A(A[14]), .B(B[14]), .Cin(_13), .S(S[14]), .Cout(_14));
  full_adder full_adder_14 (.A(A[1]), .B(B[1]), .Cin(_1), .S(S[1]), .Cout(_2));
  full_adder full_adder_15 (.A(A[15]), .B(B[15]), .Cin(_14), .S(S[15]), .Cout(COUT));
  full_adder full_adder_16 (.A(A[0]), .B(B[0]), .Cin(CIN), .S(S[0]), .Cout(_1));
endmodule
